# Fritzing sketch PCB design (saved by Fritzing 0.9.1b)
circuit board: 11.6cm x 11cm
breadboards: 1

parts:
  555 = 555 Timer [package="DIP8 [THT]"]
  R1 = Resistor [tolerance=±5% resistance=100k package=THT]
  Q1 = NPN-Transistor [part_number=2N3904 package="TO92 [THT]"]
  L1 = Inductor [inductance=10mH package="400 mil [THT]"]
  R2 = Resistor [tolerance=±5% resistance=1k package=THT]
  R3 = Resistor [tolerance=±5% resistance=100 package=THT]
  R5 = Resistor [tolerance=±5% resistance=1k package=THT]
  D1 = Rectifier Diode [part_number=1N4148 package="300 mil [THT]"]
  R6 = Resistor [tolerance=±5% resistance=220k package=THT]
  D2 = Rectifier Diode [part_number=BA159 package="300 mil [THT]"]
  D3 = Rectifier Diode [part_number=BA159 package="300 mil [THT]"]
  D4 = Rectifier Diode [part_number=BA159 package="300 mil [THT]"]
  R7 = Resistor [tolerance=±5% resistance=4.7M package=THT]
  R8 = Resistor [tolerance=±5% resistance=4.7M package=THT]
  Q3 = NPN-Transistor [part_number=2N3904 package="TO92 [THT]"]
  Q4 = NPN-Transistor [part_number=2N3904 package="TO92 [THT]"]
  R11 = Resistor [tolerance=±5% resistance=10k package=THT]
  R12 = Resistor [tolerance=±5% resistance=10k package=THT]
  J5 = female pin header, 1 pin [form="♀ (female)"]
  R4 = Trimmer Potentiometer [maximum_resistance=100Ω package=THT]
  J1 = female pin header, 1 pin [form="♀ (female)"]
  J7 = female pin header, 1 pin [form="♀ (female)"]
  R13 = Resistor [tolerance=±5% resistance=22k package=THT]
  R14 = Resistor [tolerance=±5% resistance=22k package=THT]
  R15 = Resistor [tolerance=±5% resistance=100k package=THT]
  R16 = Resistor [tolerance=±5% resistance=100k package=THT]
  J8 = female pin header, 1 pin [form="♀ (female)"]
  J9 = female pin header, 1 pin [form="♀ (female)"]
  J10 = female pin header, 1 pin [form="♀ (female)"]
  J11 = female pin header, 1 pin [form="♀ (female)"]
  J12 = female pin header, 1 pin [form="♀ (female)"]
  J13 = female pin header, 1 pin [form="♀ (female)"]
  J14 = female pin header, 1 pin [form="♀ (female)"]
  Atmega328 = atmega328 [package=dip]
  GY1 = MPU-6050 Board GY-521 [form="♀ (female)" package=THT]
  XTAL1 = Crystal [frequency="16 Mhz" package=THT]
  J15 = male pin header, 3 pins [form="♂ (male)"]
  IN_+ = SIP - 2 pins [chip_label=SVR package="SIP (Single Inline) [THT]"]
  IN_- = SIP - 2 pins [chip_label=SVR package="SIP (Single Inline) [THT]"]
  OUT_+ = SIP - 2 pins [chip_label=SVR package="SIP (Single Inline) [THT]"]
  OUT_- = SIP - 2 pins [chip_label=SVR package="SIP (Single Inline) [THT]"]
  Pad1 = Pad [width=51.2757403072259 height=18.0569805984708 connect=center]
  Pad2 = Pad [width=51.2757403072259 height=18.0569805984708 connect=center]
  R17 = Resistor [tolerance=±5% resistance=1k package=THT]
  C8 = Capacitor [part_number=0.01uF package=cap-pth-large]
  VCC2 = Battery [part_number=7.2V]
  MicroSD = IC, SIP package, 6 pins [chip_label=MicroSD]
  Q2 = npn-Powertransistor [package="TO220 [THT]"]
  C9 = Capacitor [part_number=220pF package=cap-pth-large]
  C10 = Capacitor [part_number=220pF package=cap-pth-large]
  C1 = Ceramic Capacitor [capacitance=1nF package="200 mil [THT, multilayer]"]
  LED1 = LED - 5mm [color="Red (633nm)" package="5 mm [THT]"]
  GPS = IC, SIP package, 4 pins [chip_label=GPS]
  R18 = Resistor [tolerance=±5% resistance=10k package=THT]
  S1 = Pushbutton [package="[THT]"]
  J16 = male pin header, 1 pin [form="♂ (male)"]
  J17 = male pin header, 1 pin [form="♂ (male)"]
  C6 = Ceramic Capacitor [capacitance=22pF package="200 mil [THT, multilayer]"]
  C5 = Ceramic Capacitor [capacitance=22pF package="200 mil [THT, multilayer]"]
  SN7460 = IC, DIP package, 14 pins [chip_label=SN7460]

nets:
  GND: 555.Ground, 555.Threshold, Q1.E, R6.Pin_1, Q3.E, Q4.E, R4.leg2, R15.Pin_1, R16.Pin_1, Atmega328.GND, GY1.pin2, J15.pin1, OUT_-.pin1, OUT_-.pin2, R17.Pin_0, C8.2, MicroSD.pin6, C9.2, C10.2, C1.0, GPS.pin4, S1.Pin_1, S1.Pin_2, C6.0, C5.0, SN7460.pin7
  N1: 555.Trigger, D1.cathode, R6.Pin_0, C1.1
  N2: 555.Output, R2.Pin_0, R5.Pin_0
  N3: 555.Reset, R1.Pin_1, Q1.C
  N4: 555.Discharge, R2.Pin_1, Q2.base
  5V: 555.Vcc_Supply_Voltage, R1.Pin_0, L1.pin_0, R11.Pin_1, R12.Pin_0, Atmega328.VCC, Atmega328.AVCC, GY1.pin1, OUT_+.pin1, OUT_+.pin2, MicroSD.pin5, GPS.pin1, R18.Pin_0, SN7460.pin14
  N5: Q1.B, R3.Pin_0, Q2.emitter
  N6: L1.pin_1, D2.anode, Q2.collector
  N7: R3.Pin_1, R4.leg1, R4.wiper
  N8: R5.Pin_1, D1.anode
  N9: D2.cathode, D3.anode, D4.anode, C8.1
  N10: D3.cathode, R7.Pin_0
  N11: D4.cathode, R8.Pin_0
  N12: R7.Pin_1, J7.pin1
  N13: R8.Pin_1, J5.pin1
  N14: Q3.B, R13.Pin_1, R15.Pin_0
  N15: Q3.C, R12.Pin_1, Atmega328.D8, SN7460.pin1, SN7460.pin2
  N16: Q4.B, R14.Pin_1, R16.Pin_0
  N17: Q4.C, R11.Pin_0, Atmega328.D7, SN7460.pin3, SN7460.pin13
  N18: J1.pin1, R13.Pin_0, J8.pin1, J9.pin1, J10.pin1, Pad1.pad, C9.1
  N19: R14.Pin_0, J11.pin1, J12.pin1, J13.pin1, J14.pin1, Pad2.pad, C10.1
  N20: Atmega328.RESET, R18.Pin_1, S1.Pin_3, S1.Pin_4
  N21: Atmega328.D0_(RX), J15.pin2
  N22: Atmega328.D1_(TX), J15.pin3
  N23: Atmega328.D2, GPS.pin2
  N24: Atmega328.D3_(PWM), GPS.pin3
  N25: Atmega328.D4, J17.pin1
  N26: Atmega328.XLAT1, XTAL1.pin_0, C6.1
  N27: Atmega328.XLAT2, XTAL1.pin_1, C5.1
  N28: Atmega328.D5_(PWM), LED1.anode
  N29: Atmega328.D6_(PWM), SN7460.pin11
  N30: Atmega328.D9_(PWM), J16.pin1
  N31: Atmega328.D10_(PWM), MicroSD.pin1
  N32: Atmega328.D11_(PWM), MicroSD.pin3
  N33: Atmega328.D12, MicroSD.pin4
  N34: Atmega328.D13, MicroSD.pin2
  N35: Atmega328.A4, GY1.pin4
  N36: Atmega328.A5, GY1.pin3
  N37: IN_+.pin1, IN_+.pin2, VCC2.+
  N38: IN_-.pin1, IN_-.pin2, VCC2.-
  N39: R17.Pin_1, LED1.cathode

notes:
  GM1
  GM2
  Cosmic ray detector

custom parts:
  MPU-6050 Board GY-521: Acelerometro y Giroscopio MPU-6050 Board GY-521
